// Logisim project ula2.circ as structural Verilog: 5 circuits, main circuit meio somador
// MS
module meio_somador (
  input  X,
  input  Y,
  output Sum,
  output Cout
);

  xor xor_1 (Sum, X, Y);
  and and_1 (Cout, Y, X);
endmodule

// SC
module somador_completo (
  input  Cin,
  input  X,
  input  Y,
  output Sum,
  output Cout
);

  wire meio_somador_1_cout, meio_somador_1_sum, meio_somador_2_cout;

  meio_somador meio_somador_1 (.X(X), .Y(Y), .Sum(meio_somador_1_sum), .Cout(meio_somador_1_cout));
  meio_somador meio_somador_2 (.X(Cin), .Y(meio_somador_1_sum), .Sum(Sum), .Cout(meio_somador_2_cout));
  or OR (Cout, meio_somador_2_cout, meio_somador_1_cout);
endmodule

module EA (
  input  bi,
  input  S0,
  input  S1,
  input  M,
  output yi
);

  wire and_1_out, and_2_out, not_1_out, not_2_out, not_3_out;

  not not_1 (not_1_out, S0);
  not not_2 (not_2_out, S1);
  and and_1 (and_1_out, M, not_2_out, bi);
  or or_1 (yi, and_1_out, and_2_out);
  not not_3 (not_3_out, bi);
  and and_2 (and_2_out, M, not_1_out, not_3_out);
endmodule

module EL (
  input  ai,
  input  bi,
  input  S0,
  input  S1,
  input  M,
  output xi
);

  wire and_1_out, and_2_out, and_3_out, and_4_out, and_5_out, not_1_out, not_2_out, not_3_out, not_4_out,
       or_1_out, or_3_out;

  not not_1 (not_1_out, S0);
  not not_2 (not_2_out, S1);
  not not_3 (not_3_out, M);
  and and_1 (and_1_out, not_3_out, not_2_out, not_1_out, not_4_out);
  not not_4 (not_4_out, ai);
  and and_2 (and_2_out, not_3_out, S1, S0, bi);
  or or_1 (or_1_out, and_1_out, and_2_out, and_3_out);
  and and_3 (and_3_out, not_3_out, S0, ai, bi);
  or or_2 (xi, or_1_out, or_3_out);
  and and_4 (and_4_out, not_3_out, S1, ai);
  or or_3 (or_3_out, and_4_out, and_5_out);
  and and_5 (and_5_out, M, ai);
endmodule

module ULA (
  input  a3,
  input  b3,
  input  a2,
  input  b2,
  input  a1,
  input  b1,
  input  a0,
  input  b0,
  input  S0,
  input  S1,
  input  M,
  output c4,
  output out_13,
  output f2,
  output f1,
  output f0,
  output overflow
);

  wire and_1_out, ea_1_yi, ea_2_yi, ea_3_yi, ea_4_yi, el_1_xi, el_2_xi, el_3_xi, el_4_xi,
       somador_completo_2_cout, somador_completo_3_cout, somador_completo_4_cout;

  xor xor_1 (overflow, somador_completo_2_cout, c4);
  EL el_1 (.bi(b3), .S0(S0), .S1(S1), .M(M), .xi(el_1_xi), .ai(a3));
  somador_completo somador_completo_1 (
    .Cin(somador_completo_2_cout), .X(el_1_xi), .Y(ea_1_yi), .Sum(out_13), .Cout(c4));
  EA ea_1 (.S0(S0), .S1(S1), .M(M), .bi(b3), .yi(ea_1_yi));
  somador_completo somador_completo_2 (
    .Cin(somador_completo_3_cout), .X(el_2_xi), .Y(ea_2_yi), .Sum(f2), .Cout(somador_completo_2_cout));
  EA ea_2 (.S0(S0), .S1(S1), .M(M), .bi(b2), .yi(ea_2_yi));
  EL el_2 (.bi(b2), .S0(S0), .S1(S1), .M(M), .xi(el_2_xi), .ai(a2));
  somador_completo somador_completo_3 (
    .Cin(somador_completo_4_cout), .X(el_3_xi), .Y(ea_3_yi), .Sum(f1), .Cout(somador_completo_3_cout));
  EA ea_3 (.S0(S0), .S1(S1), .M(M), .bi(b1), .yi(ea_3_yi));
  EL el_3 (.bi(b1), .S0(S0), .S1(S1), .M(M), .xi(el_3_xi), .ai(a1));
  EL el_4 (.bi(b0), .S0(S0), .S1(S1), .M(M), .xi(el_4_xi), .ai(a0));
  somador_completo somador_completo_4 (
    .Cin(and_1_out), .X(el_4_xi), .Y(ea_4_yi), .Sum(f0), .Cout(somador_completo_4_cout));
  EA ea_4 (.S0(S0), .S1(S1), .M(M), .bi(b0), .yi(ea_4_yi));
  and and_1 (and_1_out, S1, M);
endmodule
